# Fritzing sketch Projeto_timer (saved by Fritzing 0.9.3b)
circuit board: 8.46667cm x 5.64444cm
perfboards: 1

parts:
  U1 = ATmega 328P [package=dip]
  HLK-PM1 = HLK-PM01
  C3 = Ceramic Capacitor [capacitance=22pF package="100 mil [THT, multilayer]"]
  C4 = Ceramic Capacitor [capacitance=22pF package="100 mil [THT, multilayer]"]
  XTAL1 = Crystal [frequency="16 Mhz" package=THT]
  J1 = female pin header, 2 pins [form="♀ (female)"]
  J2 = female pin header, 2 pins [form="♀ (female)"]
  J3 = female pin header, 2 pins [form="♀ (female)"]
  J4 = female pin header, 2 pins [form="♀ (female)"]
  S1 = Pushbutton [package="[THT]"]
  R1 = Resistor [tolerance=±5% resistance=10k package="0603 [SMD]"]
  R2 = Resistor [tolerance=±5% resistance=150 package="0805 [SMD]"]
  LED1 = LED - 5mm [color="Green (570nm)" package="5 mm [THT]"]
  J5 = female pin header, 2 pins [form="♀ (female)"]
  R3 = Resistor [tolerance=±5% resistance=470 package="0805 [SMD]"]
  LED2 = LED - 5mm [color="Red (633nm)" package="5 mm [THT]"]
  JP1 = Header 2 [package=molex-1x2_lock]

nets:
  N1: U1.PC6_(PCINT14/^RESET)_[RESET], S1.Pin_3, S1.Pin_4, R1.Pin_0
  N2: U1.PD0_(PCINT16/RXD)_[D0], J5.pin2
  N3: U1.PD1_(PCINT17/TXD)_[D1], J5.pin1
  N4: U1.PD2_(PCINT18/INT0)_[D2], LED1.anode
  N5: U1.VCC, U1.AVCC, U1.AREF, HLK-PM1.+Vo, J2.pin1, J4.pin2, R1.Pin_1, R3.Pin_1
  N6: U1.GND, HLK-PM1.-Vo, C3.0, C4.1, J2.pin2, J3.pin1, S1.Pin_1, S1.Pin_2, R2.Pin_0, LED2.cathode
  N7: U1.PB6_(PCINT6/XTAL1/TOSC1)_[XTAL1], C3.1, XTAL1.pin_0
  N8: U1.PB7_(PCINT7/XTAL2/TOSC2)_[XTAL2], C4.0, XTAL1.pin_1
  N9: U1.PC2_(ADC2/PCINT10)_[A2], J3.pin2
  N10: U1.PC3_(ADC3/PCINT11)_[A3], J4.pin1
  N11: U1.PC4_(ADC4/SDA/PCINT12)_[A4], J1.pin2
  N12: U1.PC5_(ADC5/SCL/PCINT13)_[A5], J1.pin1
  N13: HLK-PM1.AC#0, JP1.2
  N14: HLK-PM1.AC#1, JP1.1
  N15: R2.Pin_1, LED1.cathode
  N16: R3.Pin_0, LED2.anode

custom parts:
  ATmega 328P: Atmel ATmega 328P-PU Microcontroller
